// Logisim project stage3.circ as structural Verilog: 5 circuits, main circuit interface
module \interface  (
  input  in_1,
  input  in_2,
  input  in_3,
  input  in_4,
  input  in_5,
  input  in_6,
  input  in_7,
  input  in_8,
  input  in_9,
  input  in_10,
  input  in_11,
  input  in_12,
  input  in_13,
  input  in_14,
  input  in_15,
  input  in_16
);

  wire button_1_out, button_2_out, button_4_out, button_5_out, button_6_out,
       stage3_2s_complement_1_signed_bit, stage3_2s_complement_2_signed_bit;
  wire [7:0] stage1_load_n_reset_1_output_pins, stage1_load_n_reset_2_output_pins,
       stage2_addition_1_output_bits, stage3_2s_complement_1_output_bit, stage3_2s_complement_2_output_bit;

  Button button_1 (.out(button_1_out));
  Button button_2 (.out(button_2_out));
  Button button_3 ();  // open: out
  Button button_4 (.out(button_4_out));
  Button button_5 (.out(button_5_out));
  LED led_1 (.in(stage3_2s_complement_1_signed_bit));
  LED led_2 (.in(stage3_2s_complement_1_output_bit[7]));
  LED led_3 (.in(stage3_2s_complement_1_output_bit[6]));
  LED led_4 (.in(stage3_2s_complement_1_output_bit[5]));
  LED led_5 (.in(stage3_2s_complement_1_output_bit[4]));
  stage1_load_n_reset stage1_load_n_reset_1 (
    .input_pins({in_9, in_10, in_11, in_12, in_13, in_14, in_15, in_16}), .Load(button_1_out),
    .Reset(button_4_out), .output_pins(stage1_load_n_reset_1_output_pins));
  LED led_6 (.in(stage3_2s_complement_1_output_bit[3]));
  LED led_7 (.in(stage3_2s_complement_1_output_bit[2]));
  LED led_8 ();  // open: in
  stage3_2s_complement stage3_2s_complement_1 (
    .innn(stage1_load_n_reset_1_output_pins), .switch(button_5_out),
    .signed_bit(stage3_2s_complement_1_signed_bit), .output_bit(stage3_2s_complement_1_output_bit));
  LED led_9 (.in(stage3_2s_complement_1_output_bit[1]));
  LED led_10 (.in(stage3_2s_complement_1_output_bit[0]));
  LED led_11 (.in(stage2_addition_1_output_bits[7]));
  LED led_12 (.in(stage2_addition_1_output_bits[6]));
  LED led_13 (.in(stage2_addition_1_output_bits[5]));
  LED led_14 (.in(stage2_addition_1_output_bits[4]));
  Button button_6 (.out(button_6_out));
  LED led_15 (.in(stage2_addition_1_output_bits[2]));
  LED led_16 (.in(stage2_addition_1_output_bits[3]));
  LED led_17 (.in(stage3_2s_complement_2_signed_bit));
  LED led_18 (.in(stage2_addition_1_output_bits[1]));
  LED led_19 (.in(stage3_2s_complement_2_output_bit[7]));
  LED led_20 (.in(stage3_2s_complement_2_output_bit[6]));
  LED led_21 (.in(stage2_addition_1_output_bits[0]));
  LED led_22 (.in(stage3_2s_complement_2_output_bit[5]));
  LED led_23 (.in(stage3_2s_complement_2_output_bit[4]));
  LED led_24 (.in(stage3_2s_complement_2_output_bit[3]));
  stage1_load_n_reset stage1_load_n_reset_2 (
    .input_pins({in_1, in_2, in_3, in_4, in_5, in_6, in_7, in_8}), .Load(button_1_out), .Reset(button_4_out),
    .output_pins(stage1_load_n_reset_2_output_pins));
  stage3_2s_complement stage3_2s_complement_2 (
    .innn(stage1_load_n_reset_2_output_pins), .switch(button_6_out),
    .signed_bit(stage3_2s_complement_2_signed_bit), .output_bit(stage3_2s_complement_2_output_bit));
  LED led_25 (.in(stage3_2s_complement_2_output_bit[2]));
  LED led_26 (.in(stage3_2s_complement_2_output_bit[1]));
  LED led_27 (.in(stage3_2s_complement_2_output_bit[0]));
  stage2_addition stage2_addition_1 (
    .Addition(button_2_out), .input_A(stage3_2s_complement_1_output_bit),
    .input_B(stage3_2s_complement_2_output_bit), .output_bits(stage2_addition_1_output_bits));

  // Notes on the sheet:
  //   Load
  //   Add
  //   Subtract
  //   Reset
  //   +/-
  //   +/-
  //   Input A Display
  //   +/-
  //   8 bit Binary Calculator
  //   Input A
  //   Output
  //   +/-
  //   +/-
  //   Input B
  //   Input B Display
endmodule

module stage1_load_n_reset (
  input  [7:0] input_pins,
  input  Load,
  input  Reset,
  output [7:0] output_pins
);

  D_Flip_Flop d_ff_1 (.D(input_pins[0]), .clk(Load), .Q(output_pins[0]), .reset(Reset));  // open: Qn, preset
  D_Flip_Flop d_ff_2 (.D(input_pins[1]), .clk(Load), .Q(output_pins[1]), .reset(Reset));  // open: Qn, preset
  D_Flip_Flop d_ff_3 (.D(input_pins[2]), .clk(Load), .Q(output_pins[2]), .reset(Reset));  // open: Qn, preset
  D_Flip_Flop d_ff_4 (.D(input_pins[3]), .clk(Load), .Q(output_pins[3]), .reset(Reset));  // open: Qn, preset
  D_Flip_Flop d_ff_5 (.D(input_pins[4]), .clk(Load), .Q(output_pins[4]), .reset(Reset));  // open: Qn, preset
  D_Flip_Flop d_ff_6 (.D(input_pins[5]), .clk(Load), .Q(output_pins[5]), .reset(Reset));  // open: Qn, preset
  D_Flip_Flop d_ff_7 (.D(input_pins[6]), .clk(Load), .Q(output_pins[6]), .reset(Reset));  // open: Qn, preset
  D_Flip_Flop d_ff_8 (.D(input_pins[7]), .clk(Load), .Q(output_pins[7]), .reset(Reset));  // open: Qn, preset
endmodule

module stage2_addition (
  input  Addition,
  input  [7:0] input_A,
  input  [7:0] input_B,
  output [7:0] output_bits
);

  wire and_1_out, and_2_out, and_3_out, and_4_out, and_5_out, and_6_out, and_7_out, and_8_out, and_9_out,
       and_10_out, and_11_out, and_12_out, and_13_out, and_14_out, and_15_out, or_1_out, or_2_out, or_3_out,
       or_4_out, or_5_out, or_6_out, or_7_out, xor_1_out, xor_2_out, xor_3_out, xor_4_out, xor_5_out,
       xor_6_out, xor_7_out, xor_8_out, xor_9_out, xor_10_out, xor_11_out, xor_12_out, xor_13_out,
       xor_14_out, xor_15_out;

  xor xor_1 (xor_1_out, input_A[0], input_B[0]);
  and and_1 (and_1_out, input_A[0], input_B[0]);
  xor xor_2 (xor_2_out, input_A[1], input_B[1]);
  and and_2 (and_2_out, input_A[1], input_B[1]);
  xor xor_3 (xor_3_out, input_A[2], input_B[2]);
  and and_3 (and_3_out, input_A[2], input_B[2]);
  xor xor_4 (xor_4_out, input_A[3], input_B[3]);
  and and_4 (and_4_out, input_A[3], input_B[3]);
  xor xor_5 (xor_5_out, input_A[4], input_B[4]);
  and and_5 (and_5_out, input_A[4], input_B[4]);
  xor xor_6 (xor_6_out, input_A[5], input_B[5]);
  and and_6 (and_6_out, input_A[5], input_B[5]);
  xor xor_7 (xor_7_out, input_A[6], input_B[6]);
  and and_7 (and_7_out, input_A[6], input_B[6]);
  xor xor_8 (xor_8_out, input_A[7], input_B[7]);
  and and_8 (and_8_out, input_A[7], input_B[7]);
  xor xor_9 (xor_9_out, and_1_out, xor_2_out);
  and and_9 (and_9_out, and_1_out, xor_2_out);
  xor xor_10 (xor_10_out, or_1_out, xor_3_out);
  and and_10 (and_10_out, or_1_out, xor_3_out);
  xor xor_11 (xor_11_out, or_2_out, xor_4_out);
  and and_11 (and_11_out, or_2_out, xor_4_out);
  xor xor_12 (xor_12_out, or_3_out, xor_5_out);
  and and_12 (and_12_out, or_3_out, xor_5_out);
  xor xor_13 (xor_13_out, or_4_out, xor_6_out);
  and and_13 (and_13_out, or_4_out, xor_6_out);
  xor xor_14 (xor_14_out, or_5_out, xor_7_out);
  and and_14 (and_14_out, or_5_out, xor_7_out);
  xor xor_15 (xor_15_out, or_6_out, xor_8_out);
  and and_15 (and_15_out, or_6_out, xor_8_out);
  or or_1 (or_1_out, and_9_out, and_2_out);
  or or_2 (or_2_out, and_10_out, and_3_out);
  or or_3 (or_3_out, and_11_out, and_4_out);
  or or_4 (or_4_out, and_12_out, and_5_out);
  or or_5 (or_5_out, and_13_out, and_6_out);
  or or_6 (or_6_out, and_14_out, and_7_out);
  or or_7 (or_7_out, and_15_out, and_8_out);
  D_Flip_Flop d_ff_1 (.D(xor_1_out), .clk(Addition), .Q(output_bits[0]));  // open: Qn, preset, reset
  D_Flip_Flop d_ff_2 (.D(xor_9_out), .clk(Addition), .Q(output_bits[1]));  // open: Qn, preset, reset
  D_Flip_Flop d_ff_3 (.D(xor_10_out), .clk(Addition), .Q(output_bits[2]));  // open: Qn, preset, reset
  D_Flip_Flop d_ff_4 (.D(xor_11_out), .clk(Addition), .Q(output_bits[3]));  // open: Qn, preset, reset
  D_Flip_Flop d_ff_5 (.D(xor_12_out), .clk(Addition), .Q(output_bits[4]));  // open: Qn, preset, reset
  D_Flip_Flop d_ff_6 (.D(xor_13_out), .clk(Addition), .Q(output_bits[5]));  // open: Qn, preset, reset
  D_Flip_Flop d_ff_7 (.D(xor_14_out), .clk(Addition), .Q(output_bits[6]));  // open: Qn, preset, reset
  D_Flip_Flop d_ff_8 (.D(xor_15_out), .clk(Addition), .Q(output_bits[7]));  // open: Qn, preset, reset
  LED led_1 (.in(or_7_out));
endmodule

module stage3_2s_complement (
  input  [7:0] innn,
  input  switch,
  output signed_bit,
  output [7:0] output_bit
);

  wire and_1_out, and_2_out, and_3_out, and_4_out, and_5_out, and_6_out, and_7_out, not_1_out, not_2_out,
       not_3_out, not_4_out, not_5_out, not_6_out, not_7_out, not_8_out, t_ff_1_q;
  wire [7:0] xor_1_out;

  T_Flip_Flop t_ff_1 (.T(switch), .clk(switch), .Q(t_ff_1_q));  // open: Qn, reset, preset
  not not_1 (not_1_out, innn[0]);
  not not_2 (not_2_out, innn[1]);
  not not_3 (not_3_out, innn[2]);
  not not_4 (not_4_out, innn[3]);
  not not_5 (not_5_out, innn[4]);
  not not_6 (not_6_out, innn[5]);
  not not_7 (not_7_out, innn[6]);
  not not_8 (not_8_out, innn[7]);
  xor xor_1 (xor_1_out[0], 1'b1, not_1_out);
  and and_1 (and_1_out, 1'b1, not_1_out);
  xor xor_2 (xor_1_out[1], and_1_out, not_2_out);
  and and_2 (and_2_out, and_1_out, not_2_out);
  xor xor_3 (xor_1_out[2], and_2_out, not_3_out);
  and and_3 (and_3_out, and_2_out, not_3_out);
  xor xor_4 (xor_1_out[3], and_3_out, not_4_out);
  and and_4 (and_4_out, and_3_out, not_4_out);
  xor xor_5 (xor_1_out[4], and_4_out, not_5_out);
  and and_5 (and_5_out, and_4_out, not_5_out);
  xor xor_6 (xor_1_out[5], and_5_out, not_6_out);
  and and_6 (and_6_out, and_5_out, not_6_out);
  xor xor_7 (xor_1_out[6], and_6_out, not_7_out);
  and and_7 (and_7_out, and_6_out, not_7_out);
  xor xor_8 (xor_1_out[7], and_7_out, not_8_out);
  // AND_Gate and_8 has open pins: in0=and_7_out, in1=not_8_out, out=open
  stage3_switching_signed_and_unsigned stage3_switching_signed_and_unsigned_1 (
    .switch_in(t_ff_1_q), .unsigned_number(innn), .signed_number(xor_1_out), .signed_bit(signed_bit),
    .output_bit(output_bit));
endmodule

module stage3_switching_signed_and_unsigned (
  input  switch_in,
  input  [7:0] unsigned_number,
  input  [7:0] signed_number,
  output signed_bit,
  output [7:0] output_bit
);

  wire and_1_out, and_2_out, and_3_out, and_4_out, and_5_out, and_6_out, and_7_out, and_8_out, and_9_out,
       and_10_out, and_11_out, and_12_out, and_13_out, and_14_out, and_15_out, and_16_out, not_1_out,
       not_2_out, not_3_out, not_4_out, not_5_out, not_6_out, not_7_out, not_8_out;

  not not_1 (not_1_out, switch_in);
  not not_2 (not_2_out, switch_in);
  not not_3 (not_3_out, switch_in);
  not not_4 (not_4_out, switch_in);
  not not_5 (not_5_out, switch_in);
  not not_6 (not_6_out, switch_in);
  not not_7 (not_7_out, switch_in);
  not not_8 (not_8_out, switch_in);
  and and_1 (and_1_out, unsigned_number[0], not_1_out);
  and and_2 (and_2_out, unsigned_number[1], not_2_out);
  and and_3 (and_3_out, unsigned_number[2], not_3_out);
  and and_4 (and_4_out, unsigned_number[3], not_4_out);
  and and_5 (and_5_out, unsigned_number[4], not_5_out);
  and and_6 (and_6_out, unsigned_number[5], not_6_out);
  and and_7 (and_7_out, unsigned_number[6], not_7_out);
  and and_8 (and_8_out, unsigned_number[7], not_8_out);
  and and_9 (and_9_out, signed_number[0], switch_in);
  and and_10 (and_10_out, signed_number[1], switch_in);
  and and_11 (and_11_out, signed_number[2], switch_in);
  and and_12 (and_12_out, signed_number[3], switch_in);
  and and_13 (and_13_out, signed_number[4], switch_in);
  and and_14 (and_14_out, signed_number[5], switch_in);
  and and_15 (and_15_out, signed_number[6], switch_in);
  and and_16 (and_16_out, signed_number[7], switch_in);
  or or_1 (output_bit[0], and_1_out, and_9_out);
  or or_2 (output_bit[1], and_2_out, and_10_out);
  or or_3 (output_bit[2], and_3_out, and_11_out);
  or or_4 (output_bit[3], and_4_out, and_12_out);
  or or_5 (output_bit[4], and_5_out, and_13_out);
  or or_6 (output_bit[5], and_6_out, and_14_out);
  or or_7 (output_bit[6], and_7_out, and_15_out);
  or or_8 (output_bit[7], and_8_out, and_16_out);

  assign signed_bit = switch_in;
endmodule
